# Fritzing sketch Fritzing Sketch (saved by Fritzing 0.9.5d)
circuit board: 8.46667cm x 5.64444cm
breadboards: 1

parts:
  ESP1 = ESP32-DevkitC
  RY1(-) = srd-05vdc-sl-c
  M1 = DC Motor
  RY2(+) = srd-05vdc-sl-c
  Q1(正転) = NPN-Transistor [package="TO92 [THT]"]
  Q2(逆転) = NPN-Transistor [package="TO92 [THT]"]
  Power_plug1 = Power plug
  R1 = Resistor [tolerance=±5% resistance=5.5k package=THT]
  R3 = Resistor [tolerance=±5% resistance=166 package=THT]
  R4 = Resistor [tolerance=±5% resistance=166 package=THT]
  R2 = Resistor [tolerance=±5% resistance=5.5k package=THT]

nets:
  N1: ESP1.GND, RY1(-).pin_4, RY2(+).pin_4
  N2: ESP1.IO0, R1.Pin_0
  N3: ESP1.IO2, R2.Pin_0
  N4: ESP1.5V, Q1(正転).C, Q2(逆転).C
  N5: RY1(-).pin_1, R3.Pin_1
  N6: RY1(-).pin_2, M1.pin_2, RY2(+).pin_2
  N7: RY1(-).pin_3, M1.pin_1, RY2(+).pin_3
  N8: RY1(-).pin_5, Power_plug1.GND
  N9: RY2(+).pin_1, R4.Pin_1
  N10: RY2(+).pin_5, Power_plug1.VCC
  N11: Q1(正転).E, R3.Pin_0
  N12: Q1(正転).B, R1.Pin_1
  N13: Q2(逆転).E, R4.Pin_0
  N14: Q2(逆転).B, R2.Pin_1

notes:
  コイル0.5Wくらい 5V 0.1A
  GPIO: ~40mA
  トランジスタの抵抗器どうするんや
  物理室に超高出力モータードライバICないかな〜()

custom parts:
  Power plug: 秋月電子通商 AE-DC-POWER-JACK-DIP(通販コードK-05148)とその互換品
